# Fritzing sketch BleCar (saved by Fritzing 0.9.3b)
breadboards: 1

parts:
  Part1 = Adafruit HUZZAH32 ESP32 Feather [part_number="Adafruit #3405"]
  HC-SR04_Sensor_1 = HC-SR04 Ultrasonic Distance Sensor
  S1 = H-Bridge with L298N
  J1 = Basic Servo
  BAT1 = BC9VPC [package=bc9vpc]
  M1 = DC Motor
  M2 = DC Motor
  U1 = SWITCH_SPDT [package=kps-1290]
  Part2 = Lithium Ion Polymer Battery 3.7v 500mAh [part_number=1578]  # not connected

nets:
  N1: Part1.IO21, J1.pulse
  N2: Part1.A5_IO4, S1.ENA
  N3: Part1.A1_DAC1, Part1.IO13_A12, S1.IN1, S1.IN4
  GND: Part1.GND, HC-SR04_Sensor_1.GND, S1.GND, J1.gnd, BAT1.V-
  N4: Part1.IO27_A10, S1.IN2
  N5: Part1.IO33_A9, S1.IN3
  N6: Part1.IO15_A8, HC-SR04_Sensor_1.TRIG
  N7: Part1.IO32_A7, S1.ENB
  N8: Part1.IO14_A6, HC-SR04_Sensor_1.ECHO
  VCC: HC-SR04_Sensor_1.VCC, S1.5V, J1.vcc
  N9: S1.12V, U1.S
  N10: S1.M1-01, M1.pin_2
  N11: S1.M1-02, M1.pin_1
  N12: S1.M2-01, M2.pin_2
  N13: S1.M2-02, M2.pin_1
  N14: BAT1.V+, U1.O

custom parts:
  H-Bridge with L298N: h-bridge
  Lithium Ion Polymer Battery 3.7v 500mAh: Lithium ion polymer (also known as 'lipo' or 'lipoly') batteries are thin, light and powerful. The output ranges from 4.2V when completely charged to 3.7V. This battery has a capacity of 500mAh for a total of about 1.9 Wh. The batteries come pre-attached with a genuine 2-pin JST-PH connector as shown and include the necessary protection circuitry.
